// Logisim project project3.circ as structural Verilog: 2 circuits, main circuit Control Unit
module Control_Unit (
);

  wire ADDRMODE, and_1_out, and_2_out, and_3_out, and_4_out, and_5_out, and_6_out, and_7_out, and_8_out,
       and_9_out, and_10_out, and_11_out, and_12_out, and_13_out, and_14_out, and_15_out, and_16_out,
       and_17_out, and_18_out, and_19_out, and_20_out, and_21_out, and_22_out, and_23_out, and_24_out,
       and_25_out, and_26_out, and_27_out, and_28_out, and_29_out, and_30_out, and_31_out, and_32_out,
       and_33_out, and_34_out, and_35_out, and_37_out, and_39_out, and_40_out, and_41_out, and_42_out,
       and_43_out, and_44_out, and_45_out, and_46_out, and_47_out, and_48_out, and_49_out, and_50_out,
       and_51_out, and_52_out, and_53_out, and_54_out, and_55_out, and_56_out, and_57_out, and_58_out,
       and_59_out, and_60_out, and_61_out, and_62_out, and_63_out, and_64_out, and_65_out, and_66_out,
       and_67_out, and_68_out, and_69_out, and_70_out, and_71_out, and_72_out, and_73_out, and_74_out,
       and_75_out, and_76_out, and_77_out, and_78_out, and_79_out, and_80_out, and_81_out, and_82_out,
       and_83_out, and_84_out, and_85_out, and_87_out, and_89_out, and_90_out, and_91_out, and_92_out,
       and_93_out, and_94_out, and_95_out, and_96_out, and_97_out, and_98_out, and_99_out, and_100_out,
       ARFARF, D00, D0A, D0B, D0C, D0D, D0E, D01, D02, D03, D04, D05, D06, D07, D08, D09, decoder_2_out6,
       decoder_2_out7, decoder_3_out6, decoder_3_out7, decoder_4_out6, decoder_4_out7, decoder_5_out6,
       decoder_5_out7, IR_Enable, IR_LH, Mem_clr, Mem_load, Mem_sel, Mem_str, nand_1_out, nand_2_out,
       nand_3_out, nand_4_out, nand_5_out, nand_6_out, nand_7_out, nand_8_out, nor_1_out, nor_2_out,
       nor_3_out, nor_4_out, nor_5_out, nor_6_out, nor_7_out, nor_8_out, nor_9_out, nor_10_out, nor_11_out,
       nor_12_out, not_1_out, not_2_out, not_3_out, not_4_out, not_5_out, not_6_out, not_7_out, not_8_out,
       not_9_out, not_10_out, not_11_out, not_12_out, or_1_out, or_2_out, or_3_out, or_4_out, or_5_out,
       or_6_out, or_7_out, or_8_out, or_9_out, or_10_out, or_12_out, or_13_out, or_15_out, or_16_out,
       or_17_out, or_18_out, or_19_out, or_20_out, or_21_out, or_22_out, or_23_out, or_25_out, or_27_out,
       or_28_out, SC_Reset, T0, T1, T2, T3, T4, T5, T6, T7, Z;
  wire [1:0] AR_FunSel, AR_OutCSel, IR_FunSel, MuxASel, MuxBSel, RF_FunSel, RF_OutASel, RF_OutBSel;
  wire [2:0] AR_RegSel, controlled_buffer_66_out, controlled_buffer_73_out, controlled_buffer_127_out,
       controlled_buffer_135_out, or_11_out, or_14_out, or_24_out, or_26_out;
  wire [2:1] DESTREG;
  wire [3:0] ALU_FunSel, decoder_2_out3, decoder_3_out3, decoder_4_out3, decoder_5_out3, RF_RegSel;
  wire [7:0] ADDRESS;
  wire [15:11] Instruction;

  Sequence_Counter sequence_counter_1 (
    .Reset(SC_Reset), .T0(T0), .T1(T1), .T2(T2), .T3(T3), .T4(T4), .T5(T5), .T6(T6), .T7(T7));
  nand nand_1 (nand_1_out, ADDRESS[2], ADDRESS[3]);
  and and_1 (and_1_out, ADDRESS[7], and_2_out);
  and and_2 (and_2_out, ADDRESS[2], ADDRESS[3]);
  and and_3 (and_3_out, and_1_out, and_7_out);
  nand nand_2 (nand_2_out, ADDRESS[2], ADDRESS[3]);
  and and_4 (and_4_out, ADDRESS[7], and_5_out);
  and and_5 (and_5_out, ADDRESS[2], ADDRESS[3]);
  and and_6 (and_6_out, and_4_out, and_10_out);
  Organization organization_1 (
    .OutASel(RF_OutASel), .FunSel(ALU_FunSel), .OutBSel(RF_OutBSel), .FunSel_2(RF_FunSel),
    .RegSel(RF_RegSel), .MuxASel(MuxASel), .MuxBSel(MuxBSel), .OutCSel(AR_OutCSel), .FunSel_3(AR_FunSel),
    .RegSel_2(AR_RegSel), .L_H(IR_LH), .Enable(IR_Enable), .FunSel_4(IR_FunSel), .in_7(Mem_str),
    .in_8(Mem_sel), .in_9(Mem_load), .in_10(Mem_clr),
    .Instruction({Instruction, DESTREG, ADDRMODE, ADDRESS}), .Z(Z));
  and and_7 (and_7_out, D00, T2);
  and and_8 (and_8_out, ADDRESS[7], nand_1_out);
  and and_9 (and_9_out, and_8_out, and_7_out);
  assign RF_RegSel = and_3_out ? 4'b0010 : 4'bz;  // Controlled_Buffer controlled_buffer_1
  or or_1 (or_1_out, and_3_out, and_9_out);
  and and_10 (and_10_out, D01, T2);
  and and_11 (and_11_out, ADDRESS[7], nand_2_out);
  and and_12 (and_12_out, and_11_out, and_10_out);
  assign RF_RegSel = and_6_out ? 4'b0010 : 4'bz;  // Controlled_Buffer controlled_buffer_2
  or or_2 (or_2_out, and_6_out, and_12_out);
  assign RF_FunSel = or_1_out ? 2'b00 : 2'bz;  // Controlled_Buffer controlled_buffer_3
  assign AR_OutCSel = or_1_out ? ADDRESS[6:5] : 2'bz;  // Controlled_Buffer controlled_buffer_4
  assign MuxASel = or_1_out ? 2'b10 : 2'bz;  // Controlled_Buffer controlled_buffer_5
  assign Mem_str = D00 ? 1'b0 : 1'bz;  // Controlled_Buffer controlled_buffer_6
  assign Mem_load = D00 ? 1'b1 : 1'bz;  // Controlled_Buffer controlled_buffer_7
  assign Mem_clr = D00 ? 1'b0 : 1'bz;  // Controlled_Buffer controlled_buffer_8
  assign Mem_sel = D00 ? 1'b0 : 1'bz;  // Controlled_Buffer controlled_buffer_9
  assign RF_FunSel = or_2_out ? 2'b00 : 2'bz;  // Controlled_Buffer controlled_buffer_10
  assign AR_OutCSel = or_2_out ? ADDRESS[6:5] : 2'bz;  // Controlled_Buffer controlled_buffer_11
  assign MuxASel = or_2_out ? 2'b10 : 2'bz;  // Controlled_Buffer controlled_buffer_12
  assign Mem_str = D01 ? 1'b0 : 1'bz;  // Controlled_Buffer controlled_buffer_13
  assign Mem_load = D01 ? 1'b1 : 1'bz;  // Controlled_Buffer controlled_buffer_14
  assign Mem_clr = D01 ? 1'b0 : 1'bz;  // Controlled_Buffer controlled_buffer_15
  assign Mem_sel = D01 ? 1'b0 : 1'bz;  // Controlled_Buffer controlled_buffer_16
  assign RF_RegSel = and_9_out ? 4'b0001 : 4'bz;  // Controlled_Buffer controlled_buffer_17
  assign RF_RegSel = and_12_out ? 4'b0001 : 4'bz;  // Controlled_Buffer controlled_buffer_18
  nor nor_1 (nor_1_out, ADDRESS[5], ADDRESS[6]);
  nor nor_2 (nor_2_out, ADDRESS[5], ADDRESS[6]);
  or or_3 (or_3_out, ADDRESS[5], ADDRESS[6]);
  and and_13 (and_13_out, ADDRESS[4], nor_1_out);
  and and_14 (and_14_out, and_13_out, and_17_out);
  assign RF_RegSel = and_14_out ? 4'b0100 : 4'bz;  // Controlled_Buffer controlled_buffer_19
  or or_4 (or_4_out, ADDRESS[5], ADDRESS[6]);
  and and_15 (and_15_out, ADDRESS[4], nor_2_out);
  and and_16 (and_16_out, and_15_out, and_20_out);
  assign RF_RegSel = and_16_out ? 4'b0100 : 4'bz;  // Controlled_Buffer controlled_buffer_20
  and and_17 (and_17_out, D00, T3);
  and and_18 (and_18_out, ADDRESS[4], or_3_out);
  and and_19 (and_19_out, and_18_out, and_17_out);
  or or_5 (or_5_out, and_14_out, and_19_out);
  and and_20 (and_20_out, D01, T3);
  and and_21 (and_21_out, ADDRESS[4], or_4_out);
  and and_22 (and_22_out, and_21_out, and_20_out);
  or or_6 (or_6_out, and_16_out, and_22_out);
  assign IR_LH = T0 ? 1'b0 : 1'bz;  // Controlled_Buffer controlled_buffer_21
  assign IR_Enable = T0 ? 1'b1 : 1'bz;  // Controlled_Buffer controlled_buffer_22
  assign IR_FunSel = T0 ? 2'b00 : 2'bz;  // Controlled_Buffer controlled_buffer_23
  assign Mem_load = T0 ? 1'b1 : 1'bz;  // Controlled_Buffer controlled_buffer_24
  assign Mem_str = T0 ? 1'b0 : 1'bz;  // Controlled_Buffer controlled_buffer_25
  assign Mem_sel = T0 ? 1'b0 : 1'bz;  // Controlled_Buffer controlled_buffer_26
  assign Mem_clr = T0 ? 1'b0 : 1'bz;  // Controlled_Buffer controlled_buffer_27
  assign AR_FunSel = T0 ? 2'b10 : 2'bz;  // Controlled_Buffer controlled_buffer_28
  assign AR_RegSel = T0 ? 3'b001 : 3'bz;  // Controlled_Buffer controlled_buffer_29
  assign AR_OutCSel = T0 ? 2'b10 : 2'bz;  // Controlled_Buffer controlled_buffer_30
  assign RF_RegSel = and_19_out ? 4'b1000 : 4'bz;  // Controlled_Buffer controlled_buffer_31
  assign RF_FunSel = or_5_out ? 2'b00 : 2'bz;  // Controlled_Buffer controlled_buffer_32
  assign AR_OutCSel = or_5_out ? ADDRESS[3:2] : 2'bz;  // Controlled_Buffer controlled_buffer_33
  assign MuxASel = or_5_out ? 2'b10 : 2'bz;  // Controlled_Buffer controlled_buffer_34
  assign RF_RegSel = and_22_out ? 4'b1000 : 4'bz;  // Controlled_Buffer controlled_buffer_35
  assign RF_FunSel = or_6_out ? 2'b00 : 2'bz;  // Controlled_Buffer controlled_buffer_36
  assign AR_OutCSel = or_6_out ? ADDRESS[3:2] : 2'bz;  // Controlled_Buffer controlled_buffer_37
  assign MuxASel = or_6_out ? 2'b10 : 2'bz;  // Controlled_Buffer controlled_buffer_38
  Decoder #(.select(5), .enable("false")) decoder_1 (
    .out0(D00), .out1(D01), .out2(D02), .out3(D03), .out4(D04), .out5(D05), .out6(D06), .out7(D07),
    .out8(D08), .out9(D09), .out10(D0A), .out11(D0B), .out12(D0C), .out13(D0D), .out14(D0E), .sel(Instruction));  // open: out15, out16, out17, out18, out19, out20, out21, out22, out23, out24, out25, out26, out27, out28, out29, out30, out31
  assign IR_LH = T1 ? 1'b1 : 1'bz;  // Controlled_Buffer controlled_buffer_39
  assign IR_Enable = T1 ? 1'b1 : 1'bz;  // Controlled_Buffer controlled_buffer_40
  assign IR_FunSel = T1 ? 2'b00 : 2'bz;  // Controlled_Buffer controlled_buffer_41
  assign Mem_load = T1 ? 1'b1 : 1'bz;  // Controlled_Buffer controlled_buffer_42
  assign Mem_str = T1 ? 1'b0 : 1'bz;  // Controlled_Buffer controlled_buffer_43
  assign Mem_sel = T1 ? 1'b0 : 1'bz;  // Controlled_Buffer controlled_buffer_44
  assign Mem_clr = T1 ? 1'b0 : 1'bz;  // Controlled_Buffer controlled_buffer_45
  assign AR_FunSel = T1 ? 2'b10 : 2'bz;  // Controlled_Buffer controlled_buffer_46
  assign AR_RegSel = T1 ? 3'b001 : 3'bz;  // Controlled_Buffer controlled_buffer_47
  assign AR_OutCSel = T1 ? 2'b10 : 2'bz;  // Controlled_Buffer controlled_buffer_48
  and and_23 (and_23_out, ADDRESS[7], and_24_out);
  and and_24 (and_24_out, ADDRESS[2], ADDRESS[3]);
  and and_25 (and_25_out, ADDRESS[7], and_26_out);
  and and_26 (and_26_out, ADDRESS[2], ADDRESS[3]);
  and and_27 (and_27_out, and_23_out, and_35_out);
  assign RF_OutASel = and_27_out ? 2'b10 : 2'bz;  // Controlled_Buffer controlled_buffer_49
  not not_1 (not_1_out, ARFARF);
  and and_28 (and_28_out, and_25_out, and_37_out);
  assign RF_OutBSel = and_28_out ? 2'b10 : 2'bz;  // Controlled_Buffer controlled_buffer_50
  not not_2 (not_2_out, ARFARF);
  and and_29 (and_29_out, ADDRESS[7], nand_3_out);
  nand nand_3 (nand_3_out, ADDRESS[2], ADDRESS[3]);
  and and_30 (and_30_out, and_29_out, and_35_out);
  or or_7 (or_7_out, and_27_out, and_30_out);
  and and_31 (and_31_out, not_1_out, or_7_out);
  assign RF_OutBSel = and_31_out ? ADDRESS[3:2] : 2'bz;  // Controlled_Buffer controlled_buffer_51
  and and_32 (and_32_out, ADDRESS[7], nand_4_out);
  nand nand_4 (nand_4_out, ADDRESS[2], ADDRESS[3]);
  and and_33 (and_33_out, and_32_out, and_37_out);
  or or_8 (or_8_out, and_28_out, and_33_out);
  and and_34 (and_34_out, not_2_out, or_8_out);
  assign RF_OutASel = and_34_out ? ADDRESS[3:2] : 2'bz;  // Controlled_Buffer controlled_buffer_52
  assign IR_Enable = T2 ? 1'b0 : 1'bz;  // Controlled_Buffer controlled_buffer_53
  and and_35 (and_35_out, D00, T4);
  and and_36 (ARFARF, and_29_out, and_39_out);
  assign RF_OutASel = and_30_out ? 2'b11 : 2'bz;  // Controlled_Buffer controlled_buffer_54
  assign RF_RegSel = and_35_out ? decoder_2_out3 : 4'bz;  // Controlled_Buffer controlled_buffer_55
  assign AR_RegSel = and_35_out ? or_11_out : 3'bz;  // Controlled_Buffer controlled_buffer_56
  and and_37 (and_37_out, D01, T4);
  and and_38 (ARFARF, and_32_out, and_41_out);
  assign RF_OutBSel = and_33_out ? 2'b11 : 2'bz;  // Controlled_Buffer controlled_buffer_57
  assign RF_RegSel = and_37_out ? decoder_3_out3 : 4'bz;  // Controlled_Buffer controlled_buffer_58
  assign AR_RegSel = and_37_out ? or_14_out : 3'bz;  // Controlled_Buffer controlled_buffer_59
  and and_39 (and_39_out, ADDRESS[4], or_9_out);
  and and_40 (and_40_out, and_35_out, and_39_out);
  assign RF_OutBSel = and_40_out ? 2'b00 : 2'bz;  // Controlled_Buffer controlled_buffer_60
  assign MuxASel = and_35_out ? 2'b11 : 2'bz;  // Controlled_Buffer controlled_buffer_61
  assign MuxBSel = and_35_out ? 2'b11 : 2'bz;  // Controlled_Buffer controlled_buffer_62
  assign ALU_FunSel = and_35_out ? 4'b0101 : 4'bz;  // Controlled_Buffer controlled_buffer_63
  assign RF_FunSel = and_35_out ? 2'b00 : 2'bz;  // Controlled_Buffer controlled_buffer_64
  assign AR_FunSel = and_35_out ? 2'b00 : 2'bz;  // Controlled_Buffer controlled_buffer_65
  Decoder #(.select(3), .disabled(0)) decoder_2 (
    .out0(decoder_2_out3[3]), .out1(decoder_2_out3[2]), .out2(decoder_2_out3[1]), .out3(decoder_2_out3[0]),
    .out4(or_11_out[2]), .out5(or_11_out[1]), .out6(decoder_2_out6), .out7(decoder_2_out7),
    .sel(controlled_buffer_66_out), .en(and_35_out));
  assign controlled_buffer_66_out = and_35_out ? {DESTREG, ADDRMODE} : 3'bz;  // Controlled_Buffer controlled_buffer_66
  and and_41 (and_41_out, ADDRESS[4], or_12_out);
  and and_42 (and_42_out, and_37_out, and_41_out);
  assign RF_OutASel = and_42_out ? 2'b00 : 2'bz;  // Controlled_Buffer controlled_buffer_67
  assign MuxASel = and_37_out ? 2'b11 : 2'bz;  // Controlled_Buffer controlled_buffer_68
  assign MuxBSel = and_37_out ? 2'b11 : 2'bz;  // Controlled_Buffer controlled_buffer_69
  assign ALU_FunSel = and_37_out ? 4'b0110 : 4'bz;  // Controlled_Buffer controlled_buffer_70
  assign RF_FunSel = and_37_out ? 2'b00 : 2'bz;  // Controlled_Buffer controlled_buffer_71
  assign AR_FunSel = and_37_out ? 2'b00 : 2'bz;  // Controlled_Buffer controlled_buffer_72
  assign controlled_buffer_73_out = and_37_out ? {DESTREG, ADDRMODE} : 3'bz;  // Controlled_Buffer controlled_buffer_73
  Decoder #(.select(3), .disabled(0)) decoder_3 (
    .out0(decoder_3_out3[3]), .out1(decoder_3_out3[2]), .out2(decoder_3_out3[1]), .out3(decoder_3_out3[0]),
    .out4(or_14_out[2]), .out5(or_14_out[1]), .out6(decoder_3_out6), .out7(decoder_3_out7),
    .sel(controlled_buffer_73_out), .en(and_37_out));
  or or_9 (or_9_out, ADDRESS[5], ADDRESS[6]);
  and and_43 (and_43_out, and_35_out, and_45_out);
  or or_10 (or_10_out, and_40_out, and_43_out);
  or or_11 (or_11_out[0], decoder_2_out6, decoder_2_out7);
  or or_12 (or_12_out, ADDRESS[5], ADDRESS[6]);
  and and_44 (and_44_out, and_37_out, and_47_out);
  or or_13 (or_13_out, and_42_out, and_44_out);
  or or_14 (or_14_out[0], decoder_3_out6, decoder_3_out7);
  and and_45 (and_45_out, ADDRESS[4], nor_3_out);
  nor nor_3 (nor_3_out, ADDRESS[5], ADDRESS[6]);
  assign RF_OutBSel = and_43_out ? 2'b01 : 2'bz;  // Controlled_Buffer controlled_buffer_74
  not not_3 (not_3_out, ARFARF);
  and and_46 (and_46_out, or_10_out, not_3_out);
  assign RF_OutASel = and_46_out ? ADDRESS[6:5] : 2'bz;  // Controlled_Buffer controlled_buffer_75
  assign RF_OutASel = ARFARF ? 2'b11 : 2'bz;  // Controlled_Buffer controlled_buffer_76
  assign RF_OutBSel = ARFARF ? 2'b00 : 2'bz;  // Controlled_Buffer controlled_buffer_77
  and and_47 (and_47_out, ADDRESS[4], nor_4_out);
  nor nor_4 (nor_4_out, ADDRESS[5], ADDRESS[6]);
  assign RF_OutASel = and_44_out ? 2'b01 : 2'bz;  // Controlled_Buffer controlled_buffer_78
  not not_4 (not_4_out, ARFARF);
  and and_48 (and_48_out, or_13_out, not_4_out);
  assign RF_OutBSel = and_48_out ? ADDRESS[6:5] : 2'bz;  // Controlled_Buffer controlled_buffer_79
  assign RF_OutBSel = ARFARF ? 2'b11 : 2'bz;  // Controlled_Buffer controlled_buffer_80
  assign RF_OutASel = ARFARF ? 2'b00 : 2'bz;  // Controlled_Buffer controlled_buffer_81
  and and_49 (and_49_out, D00, T5);
  not not_5 (not_5_out, and_35_out);
  nor nor_5 (nor_5_out, and_46_out, and_31_out, not_5_out, ARFARF);
  assign RF_OutASel = nor_5_out ? ADDRESS[6:5] : 2'bz;  // Controlled_Buffer controlled_buffer_82
  assign RF_OutBSel = nor_5_out ? ADDRESS[3:2] : 2'bz;  // Controlled_Buffer controlled_buffer_83
  and and_50 (and_50_out, D01, T5);
  not not_6 (not_6_out, and_37_out);
  nor nor_6 (nor_6_out, and_48_out, and_34_out, not_6_out, ARFARF);
  assign RF_OutBSel = nor_6_out ? ADDRESS[6:5] : 2'bz;  // Controlled_Buffer controlled_buffer_84
  assign RF_OutASel = nor_6_out ? ADDRESS[3:2] : 2'bz;  // Controlled_Buffer controlled_buffer_85
  assign SC_Reset = and_49_out ? 1'b1 : 1'bz;  // Controlled_Buffer controlled_buffer_86
  assign SC_Reset = and_50_out ? 1'b1 : 1'bz;  // Controlled_Buffer controlled_buffer_87
  and and_51 (and_51_out, ADDRESS[2], ADDRESS[3]);
  and and_52 (and_52_out, ADDRESS[2], ADDRESS[3]);
  nand nand_5 (nand_5_out, ADDRESS[2], ADDRESS[3]);
  and and_53 (and_53_out, ADDRESS[7], and_51_out);
  and and_54 (and_54_out, and_53_out, and_57_out);
  assign RF_RegSel = and_54_out ? 4'b0010 : 4'bz;  // Controlled_Buffer controlled_buffer_88
  nand nand_6 (nand_6_out, ADDRESS[2], ADDRESS[3]);
  and and_55 (and_55_out, ADDRESS[7], and_52_out);
  and and_56 (and_56_out, and_55_out, and_60_out);
  assign RF_RegSel = and_56_out ? 4'b0010 : 4'bz;  // Controlled_Buffer controlled_buffer_89
  and and_57 (and_57_out, D0D, T2);
  and and_58 (and_58_out, ADDRESS[7], nand_5_out);
  and and_59 (and_59_out, and_58_out, and_57_out);
  or or_15 (or_15_out, and_54_out, and_59_out);
  assign RF_FunSel = or_15_out ? 2'b00 : 2'bz;  // Controlled_Buffer controlled_buffer_90
  assign AR_OutCSel = or_15_out ? ADDRESS[6:5] : 2'bz;  // Controlled_Buffer controlled_buffer_91
  assign MuxASel = or_15_out ? 2'b10 : 2'bz;  // Controlled_Buffer controlled_buffer_92
  assign Mem_str = D0D ? 1'b0 : 1'bz;  // Controlled_Buffer controlled_buffer_93
  assign Mem_load = D0D ? 1'b1 : 1'bz;  // Controlled_Buffer controlled_buffer_94
  assign Mem_clr = D0D ? 1'b0 : 1'bz;  // Controlled_Buffer controlled_buffer_95
  assign Mem_sel = D0D ? 1'b0 : 1'bz;  // Controlled_Buffer controlled_buffer_96
  and and_60 (and_60_out, D0E, T2);
  and and_61 (and_61_out, ADDRESS[7], nand_6_out);
  and and_62 (and_62_out, and_61_out, and_60_out);
  or or_16 (or_16_out, and_56_out, and_62_out);
  assign RF_FunSel = or_16_out ? 2'b00 : 2'bz;  // Controlled_Buffer controlled_buffer_97
  assign AR_OutCSel = or_16_out ? ADDRESS[6:5] : 2'bz;  // Controlled_Buffer controlled_buffer_98
  assign MuxASel = or_16_out ? 2'b10 : 2'bz;  // Controlled_Buffer controlled_buffer_99
  assign Mem_str = D0D ? 1'b0 : 1'bz;  // Controlled_Buffer controlled_buffer_100
  assign Mem_load = D0D ? 1'b1 : 1'bz;  // Controlled_Buffer controlled_buffer_101
  assign Mem_clr = D0D ? 1'b0 : 1'bz;  // Controlled_Buffer controlled_buffer_102
  assign Mem_sel = D0D ? 1'b0 : 1'bz;  // Controlled_Buffer controlled_buffer_103
  assign RF_RegSel = and_59_out ? 4'b0001 : 4'bz;  // Controlled_Buffer controlled_buffer_104
  assign RF_RegSel = and_62_out ? 4'b0001 : 4'bz;  // Controlled_Buffer controlled_buffer_105
  and and_63 (and_63_out, ADDRESS[4], nor_7_out);
  nor nor_7 (nor_7_out, ADDRESS[5], ADDRESS[6]);
  and and_64 (and_64_out, ADDRESS[4], nor_8_out);
  nor nor_8 (nor_8_out, ADDRESS[5], ADDRESS[6]);
  or or_17 (or_17_out, ADDRESS[5], ADDRESS[6]);
  and and_65 (and_65_out, and_63_out, and_67_out);
  assign RF_RegSel = and_65_out ? 4'b0100 : 4'bz;  // Controlled_Buffer controlled_buffer_106
  or or_18 (or_18_out, ADDRESS[5], ADDRESS[6]);
  and and_66 (and_66_out, and_64_out, and_70_out);
  assign RF_RegSel = and_66_out ? 4'b0100 : 4'bz;  // Controlled_Buffer controlled_buffer_107
  and and_67 (and_67_out, D0D, T3);
  and and_68 (and_68_out, ADDRESS[4], or_17_out);
  and and_69 (and_69_out, and_68_out, and_67_out);
  or or_19 (or_19_out, and_65_out, and_69_out);
  assign RF_FunSel = or_19_out ? 2'b00 : 2'bz;  // Controlled_Buffer controlled_buffer_108
  assign AR_OutCSel = or_19_out ? ADDRESS[3:2] : 2'bz;  // Controlled_Buffer controlled_buffer_109
  assign MuxASel = or_19_out ? 2'b10 : 2'bz;  // Controlled_Buffer controlled_buffer_110
  and and_70 (and_70_out, D0E, T3);
  and and_71 (and_71_out, ADDRESS[4], or_18_out);
  and and_72 (and_72_out, and_71_out, and_70_out);
  or or_20 (or_20_out, and_66_out, and_72_out);
  assign RF_FunSel = or_20_out ? 2'b00 : 2'bz;  // Controlled_Buffer controlled_buffer_111
  assign AR_OutCSel = or_20_out ? ADDRESS[3:2] : 2'bz;  // Controlled_Buffer controlled_buffer_112
  assign MuxASel = or_20_out ? 2'b10 : 2'bz;  // Controlled_Buffer controlled_buffer_113
  assign RF_RegSel = and_69_out ? 4'b1000 : 4'bz;  // Controlled_Buffer controlled_buffer_114
  assign RF_RegSel = and_72_out ? 4'b1000 : 4'bz;  // Controlled_Buffer controlled_buffer_115
  and and_73 (and_73_out, ADDRESS[2], ADDRESS[3]);
  and and_74 (and_74_out, ADDRESS[2], ADDRESS[3]);
  and and_75 (and_75_out, ADDRESS[7], and_73_out);
  and and_76 (and_76_out, and_75_out, and_85_out);
  assign RF_OutASel = and_76_out ? 2'b10 : 2'bz;  // Controlled_Buffer controlled_buffer_116
  and and_77 (and_77_out, ADDRESS[7], and_74_out);
  and and_78 (and_78_out, and_77_out, and_87_out);
  assign RF_OutASel = and_78_out ? 2'b10 : 2'bz;  // Controlled_Buffer controlled_buffer_117
  nand nand_7 (nand_7_out, ADDRESS[2], ADDRESS[3]);
  not not_7 (not_7_out, ARFARF);
  and and_79 (and_79_out, not_7_out, or_21_out);
  assign RF_OutBSel = and_79_out ? ADDRESS[3:2] : 2'bz;  // Controlled_Buffer controlled_buffer_118
  nand nand_8 (nand_8_out, ADDRESS[2], ADDRESS[3]);
  not not_8 (not_8_out, ARFARF);
  and and_80 (and_80_out, not_8_out, or_22_out);
  assign RF_OutBSel = and_80_out ? ADDRESS[3:2] : 2'bz;  // Controlled_Buffer controlled_buffer_119
  and and_81 (and_81_out, ADDRESS[7], nand_7_out);
  and and_82 (and_82_out, and_81_out, and_85_out);
  assign RF_OutASel = and_82_out ? 2'b11 : 2'bz;  // Controlled_Buffer controlled_buffer_120
  or or_21 (or_21_out, and_76_out, and_82_out);
  and and_83 (and_83_out, ADDRESS[7], nand_8_out);
  and and_84 (and_84_out, and_83_out, and_87_out);
  assign RF_OutASel = and_84_out ? 2'b11 : 2'bz;  // Controlled_Buffer controlled_buffer_121
  or or_22 (or_22_out, and_78_out, and_84_out);
  and and_85 (and_85_out, D0D, T4);
  and and_86 (ARFARF, and_81_out, and_89_out);
  assign MuxASel = and_85_out ? 2'b11 : 2'bz;  // Controlled_Buffer controlled_buffer_122
  assign MuxBSel = and_85_out ? 2'b11 : 2'bz;  // Controlled_Buffer controlled_buffer_123
  assign ALU_FunSel = and_85_out ? 4'b0001 : 4'bz;  // Controlled_Buffer controlled_buffer_124
  assign RF_FunSel = and_85_out ? 2'b00 : 2'bz;  // Controlled_Buffer controlled_buffer_125
  assign AR_FunSel = and_85_out ? 2'b00 : 2'bz;  // Controlled_Buffer controlled_buffer_126
  assign controlled_buffer_127_out = and_85_out ? {DESTREG, ADDRMODE} : 3'bz;  // Controlled_Buffer controlled_buffer_127
  assign RF_RegSel = and_85_out ? decoder_4_out3 : 4'bz;  // Controlled_Buffer controlled_buffer_128
  assign AR_RegSel = and_85_out ? or_24_out : 3'bz;  // Controlled_Buffer controlled_buffer_129
  and and_87 (and_87_out, D0E, T4);
  and and_88 (ARFARF, and_83_out, and_91_out);
  assign MuxASel = and_87_out ? 2'b11 : 2'bz;  // Controlled_Buffer controlled_buffer_130
  assign MuxBSel = and_87_out ? 2'b11 : 2'bz;  // Controlled_Buffer controlled_buffer_131
  assign ALU_FunSel = and_87_out ? 4'b0000 : 4'bz;  // Controlled_Buffer controlled_buffer_132
  assign RF_FunSel = and_87_out ? 2'b00 : 2'bz;  // Controlled_Buffer controlled_buffer_133
  assign AR_FunSel = and_87_out ? 2'b00 : 2'bz;  // Controlled_Buffer controlled_buffer_134
  assign controlled_buffer_135_out = and_87_out ? {DESTREG, ADDRMODE} : 3'bz;  // Controlled_Buffer controlled_buffer_135
  assign RF_RegSel = and_87_out ? decoder_5_out3 : 4'bz;  // Controlled_Buffer controlled_buffer_136
  assign AR_RegSel = and_87_out ? or_26_out : 3'bz;  // Controlled_Buffer controlled_buffer_137
  and and_89 (and_89_out, ADDRESS[4], or_23_out);
  or or_23 (or_23_out, ADDRESS[5], ADDRESS[6]);
  and and_90 (and_90_out, and_85_out, and_89_out);
  assign RF_OutBSel = and_90_out ? 2'b00 : 2'bz;  // Controlled_Buffer controlled_buffer_138
  Decoder #(.select(3), .disabled(0)) decoder_4 (
    .out0(decoder_4_out3[3]), .out1(decoder_4_out3[2]), .out2(decoder_4_out3[1]), .out3(decoder_4_out3[0]),
    .out4(or_24_out[2]), .out5(or_24_out[1]), .out6(decoder_4_out6), .out7(decoder_4_out7),
    .sel(controlled_buffer_127_out), .en(and_85_out));
  or or_24 (or_24_out[0], decoder_4_out6, decoder_4_out7);
  and and_91 (and_91_out, ADDRESS[4], or_25_out);
  or or_25 (or_25_out, ADDRESS[5], ADDRESS[6]);
  and and_92 (and_92_out, and_87_out, and_91_out);
  assign RF_OutBSel = and_92_out ? 2'b00 : 2'bz;  // Controlled_Buffer controlled_buffer_139
  Decoder #(.select(3), .disabled(0)) decoder_5 (
    .out0(decoder_5_out3[3]), .out1(decoder_5_out3[2]), .out2(decoder_5_out3[1]), .out3(decoder_5_out3[0]),
    .out4(or_26_out[2]), .out5(or_26_out[1]), .out6(decoder_5_out6), .out7(decoder_5_out7),
    .sel(controlled_buffer_135_out), .en(and_87_out));
  or or_26 (or_26_out[0], decoder_5_out6, decoder_5_out7);
  and and_93 (and_93_out, ADDRESS[4], nor_9_out);
  and and_94 (and_94_out, and_85_out, and_93_out);
  assign RF_OutBSel = and_94_out ? 2'b01 : 2'bz;  // Controlled_Buffer controlled_buffer_140
  or or_27 (or_27_out, and_90_out, and_94_out);
  and and_95 (and_95_out, ADDRESS[4], nor_10_out);
  and and_96 (and_96_out, and_87_out, and_95_out);
  assign RF_OutBSel = and_96_out ? 2'b01 : 2'bz;  // Controlled_Buffer controlled_buffer_141
  or or_28 (or_28_out, and_92_out, and_96_out);
  nor nor_9 (nor_9_out, ADDRESS[5], ADDRESS[6]);
  not not_9 (not_9_out, ARFARF);
  and and_97 (and_97_out, or_27_out, not_9_out);
  assign RF_OutASel = and_97_out ? ADDRESS[6:5] : 2'bz;  // Controlled_Buffer controlled_buffer_142
  assign RF_OutASel = ARFARF ? 2'b11 : 2'bz;  // Controlled_Buffer controlled_buffer_143
  assign RF_OutBSel = ARFARF ? 2'b00 : 2'bz;  // Controlled_Buffer controlled_buffer_144
  nor nor_10 (nor_10_out, ADDRESS[5], ADDRESS[6]);
  not not_10 (not_10_out, ARFARF);
  and and_98 (and_98_out, or_28_out, not_10_out);
  assign RF_OutASel = and_98_out ? ADDRESS[6:5] : 2'bz;  // Controlled_Buffer controlled_buffer_145
  assign RF_OutASel = ARFARF ? 2'b11 : 2'bz;  // Controlled_Buffer controlled_buffer_146
  assign RF_OutBSel = ARFARF ? 2'b00 : 2'bz;  // Controlled_Buffer controlled_buffer_147
  and and_99 (and_99_out, D0D, T5);
  assign SC_Reset = and_99_out ? 1'b1 : 1'bz;  // Controlled_Buffer controlled_buffer_148
  not not_11 (not_11_out, and_85_out);
  nor nor_11 (nor_11_out, and_97_out, and_79_out, not_11_out, ARFARF);
  assign RF_OutASel = nor_11_out ? ADDRESS[6:5] : 2'bz;  // Controlled_Buffer controlled_buffer_149
  assign RF_OutBSel = nor_11_out ? ADDRESS[3:2] : 2'bz;  // Controlled_Buffer controlled_buffer_150
  and and_100 (and_100_out, D0E, T5);
  assign SC_Reset = and_100_out ? 1'b1 : 1'bz;  // Controlled_Buffer controlled_buffer_151
  not not_12 (not_12_out, and_87_out);
  nor nor_12 (nor_12_out, and_98_out, and_80_out, not_12_out, ARFARF);
  assign RF_OutASel = nor_12_out ? ADDRESS[6:5] : 2'bz;  // Controlled_Buffer controlled_buffer_152
  assign RF_OutBSel = nor_12_out ? ADDRESS[3:2] : 2'bz;  // Controlled_Buffer controlled_buffer_153

  // Other names for the same wires on the sheet: Instruction[10:0] = {DESTREG, ADDRMODE, ADDRESS};
  //   SRCREG2[2:0] = ADDRESS[4:2]; SRCREG1[2:0] = ADDRESS[7:5]; DESTREG[0] = ADDRMODE; REGSEL[1:0] = DESTREG;
  //   OPCODE[4:0] = Instruction

  // Notes on the sheet:
  //   Sequence Counter
  //   ORGANIZATION
  //   D00 - ADD
  //   D01 - SUB
  //   FETCH & DECODE
  //   D0D - OR
  //   D0E - AND
endmodule

module Sequence_Counter (
  input  Reset,
  output T0,
  output T1,
  output T2,
  output T3,
  output T4,
  output T5,
  output T6,
  output T7
);

  wire clock_1_out;
  wire [2:0] counter_1_q;

  Clock clock_1 (.out(clock_1_out));
  Counter #(.width(3), .max('h7)) counter_1 (
    .count(1'b1), .Q(counter_1_q), .clk(clock_1_out), .clr(Reset));  // open: load, D, carry, preset, down
  Decoder #(.select(3), .enable("false")) decoder_1 (
    .out0(T0), .out1(T1), .out2(T2), .out3(T3), .out4(T4), .out5(T5), .out6(T6), .out7(T7), .sel(counter_1_q));
endmodule
